# Fritzing sketch IRTank (saved by Fritzing 0.9.2b)
circuit board: 8.46667cm x 5.64444cm

parts:
  Arduino_Nano = Arduino Nano (Rev3.0)
  DC-DC = IC, DIP package, 8 pins [chip_label=DC-DC]
  Motor_Driver = TB6612FNG [chip_label=TB6612FNG package="DIP (Dual Inline) [THT]"]
  BAT_MOT_1 = Battery Holders [package=battery-aaa]
  BAT_IC = Battery Holders [package=battery-aaa]
  BAT_MOT_2 = Battery Holders [package=battery-aaa]
  S1 = Toggle Switch [package=THT]
  MOT_RIGHT = DC Motor
  MOT_LEFT = DC Motor
  IR_Receiver = Infra red receiver

nets:
  GND: Arduino_Nano.GND, DC-DC.pin8, Motor_Driver.GND, BAT_IC.-, BAT_MOT_2.-, IR_Receiver.GND
  N1: Arduino_Nano.D3, Motor_Driver.PWMA
  N2: Arduino_Nano.D4, Motor_Driver.AIN2
  N3: Arduino_Nano.D5, Motor_Driver.AIN1
  N4: Arduino_Nano.D6, Motor_Driver.STBY
  N5: Arduino_Nano.D7, Motor_Driver.BIN1
  N6: Arduino_Nano.D8, Motor_Driver.BIN2
  N7: Arduino_Nano.D9, Motor_Driver.PWMB
  N8: Arduino_Nano.D10, IR_Receiver.Data
  N9: Arduino_Nano.VIN, S1.L1
  VCC: Arduino_Nano.5V, Motor_Driver.Vcc, IR_Receiver.VCC
  N10: DC-DC.pin2, S1.COM
  N11: DC-DC.pin3, DC-DC.pin6, BAT_IC.+
  N12: Motor_Driver.AO1, MOT_LEFT.pin_1
  N13: Motor_Driver.AO2, MOT_LEFT.pin_2
  N14: Motor_Driver.BO2, MOT_RIGHT.pin_2
  N15: Motor_Driver.BO1, MOT_RIGHT.pin_1
  N16: Motor_Driver.VMOT, BAT_MOT_1.+
  N17: BAT_MOT_1.-, BAT_MOT_2.+

custom parts:
  TB6612FNG: A DIP stand-in part for whatever IC you want. With 16 pins on a 600mil dual inline package (DIP) footprint.
